// Digital circuit rjstack.dig as structural Verilog
module rjstack (
  input  [15:0] i,
  input  push,
  input  pop,
  input  we_tos,
  output [15:0] ros,
  output [15:0] tos,
  output [11:0] sp,
  output [15:0] nos
);

  wire c, or_1_out;
  wire [11:0] add_1_s, multiplexer_1_out, sp_q;
  wire [15:0] multiplexer_3_out, multiplexer_4_out;

  Button clk (.out(c));
  Multiplexer #(.Bits(12)) multiplexer_1 (.sel(push), .in_0({12{1'b1}}), .in_1(12'h1), .out(multiplexer_1_out));
  Add #(.Bits(12)) add_1 (.a(sp_q), .b(multiplexer_1_out), .c_i(1'b0), .s(add_1_s));  // open: c_o
  or or_1 (or_1_out, push, pop);
  Register #(.Bits(12)) u_sp (.D(add_1_s), .C(c), .en(or_1_out), .Q(sp_q));
  Multiplexer #(.Bits(12)) multiplexer_2 (.sel(push), .in_0(add_1_s), .in_1(sp_q), .out(sp));
  Multiplexer #(.Bits(16)) multiplexer_3 (.sel(pop), .in_0(i), .in_1(nos), .out(multiplexer_3_out));
  Multiplexer #(.Bits(16)) multiplexer_4 (.sel(pop), .in_0(tos), .in_1(ros), .out(multiplexer_4_out));
  Register #(.Bits(16)) u_tos (.D(multiplexer_3_out), .C(c), .en(we_tos), .Q(tos));
  Register #(.Bits(16)) u_nos (.D(multiplexer_4_out), .C(c), .en(or_1_out), .Q(nos));
  RAMDualPort #(.AddrBits(12), .Bits(16)) stack (.A(sp), .Din(nos), .str(push), .C(c), .ld(1'b1), .D(ros));

  // Notes on the sheet:
  //   [00]
  //   FPGA Stack Machine CPU from Scratch
  //   rj45Creates
  //   Building the Stack
endmodule
